# Fritzing sketch Circuit_diagram (saved by Fritzing 0.9.3b)

parts:
  부품1 = Arduino Mega 2560 (Rev3)
  부품2 = Arduino Mega 2560 (Rev3)

nets:
  GND: 부품1.GND, 부품2.GND
  N1: 부품1.D50, 부품2.D50
  N2: 부품1.D51, 부품2.D51
  N3: 부품1.D52, 부품2.D52
  N4: 부품1.D53, 부품2.D53
